// Logisim project CircuitoFinal.circ as structural Verilog: 4 circuits, main circuit Pipeline
module DataPath1 (
  input  [3:0] ALUOp,
  input  RegWrite,
  input  ALUScr,
  input  RegDst,
  input  RST,
  output [31:0] out_6,
  output [4:0] RegB,
  output [31:0] A,
  output [4:0] RegA,
  output [31:0] B,
  output [4:0] rW
);

  wire CLK_out;
  wire [15:0] undriven;
  wire [31:0] adder_1_out, bit_extender_1_out, PC_q, registerfile_1_p7;

  Clock CLK (.out(CLK_out));
  Register #(.width(32)) PC (.D(adder_1_out), .en(1'b1), .clk(CLK_out), .Q(PC_q), .clr(RST));
  Adder #(.width(32)) adder_1 (.a(32'h4), .b(PC_q), .out(adder_1_out));  // open: cin, cout
  // MIPSProgramROM mipsprogramrom_1: pin names not known; wires that end beside it: PC_q, CLK_out
  Multiplexer #(.width(5), .enable("false")) multiplexer_1 (.in0(RegB), .in1(undriven[15:11]), .out(rW), .sel(RegDst));
  assign bit_extender_1_out = {{16{undriven[15]}}, undriven};  // Bit_Extender bit_extender_1
  // RegisterFile registerfile_1: pin names not known; wires that end beside it: out_6, RegWrite, rW, RegA, RegB, A, registerfile_1_p7
  Multiplexer #(.width(32), .enable("false")) multiplexer_2 (
    .in0(registerfile_1_p7), .in1(bit_extender_1_out), .out(B), .sel(ALUScr));
  // Mips_ALU mips_alu_1: pin names not known; wires that end beside it: A, B, ALUOp, out_6

  // Notes on the sheet:
  //   contents of mipsprogramrom_1 (hex, n*v repeats v):
  //   addiu $2, $2, 10 addu $3, $1, $2 subu $4, $2, $1
endmodule

module DataPath2 (
  input  RST,
  input  Branch,
  input  RegDst,
  input  RegWrite,
  input  ALUScr,
  input  [3:0] ALUOp,
  input  MemWrite,
  input  MemRead,
  input  MemToReg,
  output [4:0] RegB,
  output [4:0] RegA,
  output [4:0] RegW,
  output [31:0] A,
  output [31:0] B
);

  wire b_t, mips_ram_1_p5;
  wire [11:0] mips_alu_1_p4_2;
  wire [15:0] undriven;
  wire [19:0] mips_alu_1_p4;
  wire [31:0] adder_1_out, adder_2_out, bit_extender_1_out, mips_ram_1_p7, multiplexer_1_out, PC_q,
       registerfile_1_p1, registerfile_1_p7, shifter_1_out;

  Register #(.width(32)) PC (.D(multiplexer_1_out), .en(1'b1), .clk(b_t), .Q(PC_q), .clr(RST));
  Adder #(.width(32)) adder_1 (.a(32'h4), .b(PC_q), .out(adder_1_out));  // open: cin, cout
  Clock CLK (.out(b_t));
  Adder #(.width(32)) adder_2 (.a(adder_1_out), .b(shifter_1_out), .out(adder_2_out));  // open: cin, cout
  Multiplexer #(.width(32), .enable("false")) multiplexer_1 (
    .in0(adder_1_out), .in1(adder_2_out), .out(multiplexer_1_out), .sel(Branch));
  // MIPSProgramROM mipsprogramrom_1: pin names not known; wires that end beside it: PC_q, b_t
  Multiplexer #(.width(5), .enable("false")) multiplexer_2 (
    .in0(RegB), .in1(undriven[15:11]), .out(RegW), .sel(RegDst));
  assign bit_extender_1_out = {{16{undriven[15]}}, undriven};  // Bit_Extender bit_extender_1
  // RegisterFile registerfile_1: pin names not known; wires that end beside it: registerfile_1_p1, RegWrite, RegW, RegA, RegB, A, registerfile_1_p7
  Shifter #(.width(32)) shifter_1 (.in(bit_extender_1_out), .\dist (5'b00010), .out(shifter_1_out));
  // Mips_ALU mips_alu_1: pin names not known; wires that end beside it: A, B, ALUOp, {mips_alu_1_p4_2, mips_alu_1_p4}, mips_alu_1_p4, registerfile_1_p7, MemWrite
  Multiplexer #(.width(32), .enable("false")) multiplexer_3 (
    .in0(registerfile_1_p7), .in1(bit_extender_1_out), .out(B), .sel(ALUScr));
  // MIPS_RAM mips_ram_1: pin names not known; wires that end beside it: 4'b1111, b_t, MemRead, RST, mips_ram_1_p5, mips_ram_1_p5, mips_ram_1_p7
  Multiplexer #(.width(32), .enable("false")) multiplexer_4 (
    .in0({mips_alu_1_p4_2, mips_alu_1_p4}), .in1(mips_ram_1_p7), .out(registerfile_1_p1), .sel(MemToReg));

  // Other names for the same wires on the sheet: a_t = RST; c = Branch; d = RegDst; e = RegWrite; f = ALUScr;
  //   g[3:0] = ALUOp; h = MemWrite; i = MemRead; j = MemToReg

  // Notes on the sheet:
  //   contents of mipsprogramrom_1 (hex, n*v repeats v):
  //   beq $1, $2, end         lw $5, 0($3)    sw $5, 0($4)    bne $1, $2, loop end:
endmodule

module Pipeline (
  input  RST,
  input  Branch,
  input  RegDst,
  input  RegWrite,
  input  ALUScr,
  input  [3:0] ALUOp,
  input  [1:0] Forwarding_A,
  input  [1:0] Forwarding_B,
  input  MemWrite,
  input  MemRead,
  input  MemToReg,
  output [4:0] AddrB,
  output [4:0] AddrA,
  output [4:0] AddrW,
  output [31:0] A,
  output [31:0] B,
  output [5:0] out_17
);

  wire b_t, mips_ram_1_p8;
  wire [4:0] register_3_q, register_5_q, registerfile_1_p4;
  wire [15:0] IF_ID_q;
  wire [31:0] adder_1_out, adder_2_out, bit_extender_1_out, EX_MEM_q, ID_EX_q, mips_alu_1_p4, mips_ram_1_p10,
       mipsprogramrom_1_p2, multiplexer_1_out, multiplexer_3_out, multiplexer_6_out, PC_q, register_1_q,
       register_2_q, register_4_q, registerfile_1_p1, registerfile_1_p7, registerfile_1_p8, shifter_1_out;

  Register #(.width(32)) PC (.D(multiplexer_1_out), .en(1'b1), .clk(b_t), .Q(PC_q), .clr(RST));
  Adder #(.width(32)) adder_1 (.a(32'h4), .b(PC_q), .out(adder_1_out));  // open: cin, cout
  Adder #(.width(32)) adder_2 (.a(adder_1_out), .b(shifter_1_out), .out(adder_2_out));  // open: cin, cout
  Multiplexer #(.width(32), .enable("false")) multiplexer_1 (
    .in0(adder_1_out), .in1(adder_2_out), .out(multiplexer_1_out), .sel(Branch));
  Register #(.width(32)) IF_ID (
    .D(mipsprogramrom_1_p2), .en(1'b1), .clk(b_t), .Q({out_17, AddrA, AddrB, IF_ID_q}), .clr(RST));
  // MIPSProgramROM mipsprogramrom_1: pin names not known; wires that end beside it: PC_q, mipsprogramrom_1_p2
  Clock CLK (.out(b_t));
  Multiplexer #(.width(5), .enable("false")) multiplexer_2 (
    .in0(AddrB), .in1(IF_ID_q[15:11]), .out(AddrW), .sel(RegDst));
  assign bit_extender_1_out = {{16{IF_ID_q[15]}}, IF_ID_q};  // Bit_Extender bit_extender_1
  // RegisterFile registerfile_1: pin names not known; wires that end beside it: registerfile_1_p1, b_t, RegWrite, registerfile_1_p4, AddrA, AddrB, registerfile_1_p7, registerfile_1_p8
  Shifter #(.width(32)) shifter_1 (.in(bit_extender_1_out), .\dist (5'b00010), .out(shifter_1_out));
  Register #(.width(32)) ID_EX (.D(registerfile_1_p7), .en(1'b1), .clk(b_t), .Q(ID_EX_q), .clr(RST));
  Register #(.width(32)) register_1 (.D(registerfile_1_p8), .en(1'b1), .clk(b_t), .Q(register_1_q), .clr(RST));
  Register #(.width(32)) register_2 (.D(bit_extender_1_out), .en(1'b1), .clk(b_t), .Q(register_2_q), .clr(RST));
  Register #(.width(5)) register_3 (.D(AddrW), .en(1'b1), .clk(b_t), .Q(register_3_q), .clr(RST));
  Multiplexer #(.width(32), .enable("false")) multiplexer_3 (
    .in0(register_1_q), .in1(register_2_q), .out(multiplexer_3_out), .sel(ALUScr));
  Multiplexer #(.select(2), .width(32), .enable("false")) multiplexer_4 (
    .in0(ID_EX_q), .in1(EX_MEM_q), .in2(registerfile_1_p1), .out(A), .sel(Forwarding_A));  // open: in3
  Multiplexer #(.select(2), .width(32), .enable("false")) multiplexer_5 (
    .in0(multiplexer_3_out), .in1(EX_MEM_q), .in2(registerfile_1_p1), .out(B), .sel(Forwarding_B));  // open: in3
  // Mips_ALU mips_alu_1: pin names not known; wires that end beside it: A, B, ALUOp, mips_alu_1_p4
  Register #(.width(32)) EX_MEM (.D(mips_alu_1_p4), .en(1'b1), .clk(b_t), .Q(EX_MEM_q), .clr(RST));
  Register #(.width(32)) register_4 (.D(register_1_q), .en(1'b1), .clk(b_t), .Q(register_4_q), .clr(RST));
  Register #(.width(5)) register_5 (.D(register_3_q), .en(1'b1), .clk(b_t), .Q(register_5_q), .clr(RST));
  // MIPS_RAM mips_ram_1: pin names not known; wires that end beside it: EX_MEM_q[19:0], register_4_q, MemWrite, 4'b1111, b_t, MemRead, RST, mips_ram_1_p8, mips_ram_1_p8, mips_ram_1_p10
  Multiplexer #(.width(32), .enable("false")) multiplexer_6 (
    .in0(mips_ram_1_p10), .in1(EX_MEM_q), .out(multiplexer_6_out), .sel(MemToReg));
  Register #(.width(32)) MEM_WB (.D(multiplexer_6_out), .en(1'b1), .clk(b_t), .Q(registerfile_1_p1), .clr(RST));
  Register #(.width(5)) register_6 (.D(register_5_q), .en(1'b1), .clk(b_t), .Q(registerfile_1_p4), .clr(RST));

  // Other names for the same wires on the sheet: a_t = RST; c = Branch; d = RegDst; e = RegWrite; f = ALUScr;
  //   g[3:0] = ALUOp; h[1:0] = Forwarding_A; i[1:0] = Forwarding_B; j = MemWrite; k = MemRead; l = MemToReg

  // Notes on the sheet:
  //   contents of mipsprogramrom_1 (hex, n*v repeats v):
  //   sw $3, 0($2)
endmodule

module Controle (
  input  [5:0] in_1,
  input  in_2,
  output RegDST,
  output ALUScr,
  output MemToReg,
  output RegWrite,
  output MemRead,
  output MemWrite,
  output [3:0] AluOP,
  output PC,
  output Reset
);

  wire and_1_out, and_2_out, and_3_out, and_4_out, and_5_out, clock_1_out, demultiplexer_1_out2,
       demultiplexer_1_out4, demultiplexer_2_out1, demultiplexer_2_out5, demultiplexer_3_out1,
       demultiplexer_3_out3, j_k_ff_1_q, or_1_out, or_2_out;
  wire [2:0] counter_1_q;

  and and_1 (and_1_out, in_1[0], in_1[1], in_1[2], in_1[3], in_1[4], in_1[5]);
  and and_2 (and_2_out, ~in_1[0], ~in_1[1], ~in_1[2], ~in_1[3], ~in_1[4], ~in_1[5]);  // AND_Gate
  and and_3 (and_3_out, in_1[0], ~in_1[1], ~in_1[2], ~in_1[3], in_1[4], in_1[5]);  // AND_Gate
  and and_4 (and_4_out, in_1[0], ~in_1[1], in_1[2], ~in_1[3], in_1[4], in_1[5]);  // AND_Gate
  J_K_Flip_Flop j_k_ff_1 (.J(1'b1), .K(1'b1), .clk(or_1_out), .Q(j_k_ff_1_q));  // open: Qn, preset, reset
  or or_1 (or_1_out, and_1_out, in_2);
  Clock clock_1 (.out(clock_1_out));
  or or_2 (or_2_out, and_2_out, and_3_out, and_4_out);
  and and_5 (and_5_out, j_k_ff_1_q, clock_1_out);
  not not_1 (Reset, j_k_ff_1_q);
  Counter #(.width(3), .max('h7)) counter_1 (
    .clr(Reset), .count(or_2_out), .clk(and_5_out), .Q(counter_1_q));  // open: load, up, D, carry
  Demultiplexer #(.select(3), .enable("false")) demultiplexer_1 (
    .out1(RegDST), .out2(demultiplexer_1_out2), .out3(AluOP[1]), .out4(demultiplexer_1_out4), .in(and_2_out),
    .sel(counter_1_q));  // open: out0, out5, out6, out7
  Demultiplexer #(.select(3), .enable("false")) demultiplexer_2 (
    .out1(demultiplexer_2_out1), .out2(MemRead), .out3(MemToReg), .out4(RegWrite),
    .out5(demultiplexer_2_out5), .in(and_3_out), .sel(counter_1_q));  // open: out0, out6, out7
  Demultiplexer #(.select(3), .enable("false")) demultiplexer_3 (
    .out1(demultiplexer_3_out1), .out2(MemWrite), .out3(demultiplexer_3_out3), .in(and_4_out),
    .sel(counter_1_q));  // open: out0, out4, out5, out6, out7
  or or_3 (ALUScr, demultiplexer_1_out2, demultiplexer_2_out1, demultiplexer_3_out1);
  or or_4 (PC, demultiplexer_1_out4, demultiplexer_2_out5, demultiplexer_3_out3);

  assign {AluOP[3:2], AluOP[0]} = 3'b000;
endmodule
