// Logisim project LogiSim - Prática 2.circ as structural Verilog: 1 circuit, main circuit main
module main (
  input  Branch,
  input  RegWrite,
  input  [3:0] ALUOp,
  input  MemToReg,
  input  Immediate,
  input  MemWrite,
  input  MemRead,
  input  RegDst,
  input  RESET,
  output [31:0] A,
  output [31:0] B,
  output [4:0] AddrB,
  output [4:0] AddrA,
  output [4:0] AddrW
);

  wire clock_1_out, mips_ram_1_p5;
  wire [15:0] undriven;
  wire [31:0] adder_1_out, adder_2_out, bit_extender_1_out, mips_alu_1_p4, mips_ram_1_p7, multiplexer_1_out,
       PC_q, registerfile_1_p1, registerfile_1_p7, shifter_1_out;

  Register #(.width(32)) PC (.D(multiplexer_1_out), .en(1'b1), .clk(clock_1_out), .Q(PC_q), .clr(RESET));
  Clock clock_1 (.out(clock_1_out));
  Adder #(.width(32)) adder_1 (.a(32'h4), .b(PC_q), .out(adder_1_out));  // open: cin, cout
  Adder #(.width(32)) adder_2 (.a(adder_1_out), .b(shifter_1_out), .out(adder_2_out));  // open: cin, cout
  Multiplexer #(.width(32), .enable("false")) multiplexer_1 (
    .in0(adder_1_out), .in1(adder_2_out), .out(multiplexer_1_out), .sel(Branch));
  // MIPSProgramROM mipsprogramrom_1: pin names not known; wires that end beside it: PC_q, clock_1_out
  Multiplexer #(.width(5), .enable("false")) multiplexer_2 (
    .in0(AddrB), .in1(undriven[15:11]), .out(AddrW), .sel(RegDst));
  assign bit_extender_1_out = {{16{undriven[15]}}, undriven};  // Bit_Extender bit_extender_1
  // RegisterFile registerfile_1: pin names not known; wires that end beside it: registerfile_1_p1, RegWrite, AddrW, AddrA, AddrB, A, registerfile_1_p7
  Shifter #(.width(32)) shifter_1 (.in(bit_extender_1_out), .\dist (5'b00010), .out(shifter_1_out));
  Multiplexer #(.width(32), .enable("false")) multiplexer_3 (
    .in0(registerfile_1_p7), .in1(bit_extender_1_out), .out(B), .sel(Immediate));
  // Mips_ALU mips_alu_1: pin names not known; wires that end beside it: A, B, ALUOp, mips_alu_1_p4, mips_alu_1_p4[19:0], registerfile_1_p7, MemWrite
  // MIPS_RAM mips_ram_1: pin names not known; wires that end beside it: 4'b1111, clock_1_out, MemRead, RESET, mips_ram_1_p5, mips_ram_1_p5, mips_ram_1_p7
  Multiplexer #(.width(32), .enable("false")) multiplexer_4 (
    .in0(mips_ram_1_p7), .in1(mips_alu_1_p4), .out(registerfile_1_p1), .sel(MemToReg));

  // Notes on the sheet:
  //   contents of mipsprogramrom_1 (hex, n*v repeats v):
  //   subu $9,$16,$10 addu $9,$8,$8 addiu $9,$10,30
endmodule
