// Logisim project Pipeline.circ as structural Verilog: 1 circuit, main circuit main
module main (
  input  [1:0] in_1,
  input  [1:0] in_2,
  input  RegWrite,
  input  Branch,
  input  ALUScr,
  input  [3:0] ALUOp,
  input  RegDst,
  input  MemWrite,
  input  MemRead,
  input  MemToReg,
  input  RESET,
  output [31:0] A,
  output [31:0] B,
  output [4:0] AddrB,
  output [4:0] AddrA,
  output [4:0] AddrW
);

  wire clock_1_out, mips_ram_1_p8;
  wire [4:0] register_3_q, register_5_q, registerfile_1_p4;
  wire [31:0] adder_1_out, adder_2_out, bit_extender_1_out, EX_MEM_q, ID_EX_q, IF_ID_q, mips_alu_1_p4,
       mips_ram_1_p10, mipsprogramrom_1_p2, multiplexer_1_out, multiplexer_3_out, multiplexer_6_out, PC_q,
       register_1_q, register_2_q, register_4_q, registerfile_1_p1, registerfile_1_p7, registerfile_1_p8,
       shifter_1_out;

  Register #(.width(32)) PC (.D(multiplexer_1_out), .en(1'b1), .clk(clock_1_out), .Q(PC_q), .clr(RESET));
  Adder #(.width(32)) adder_1 (.a(32'h4), .b(PC_q), .out(adder_1_out));  // open: cin, cout
  Adder #(.width(32)) adder_2 (.a(adder_1_out), .b(shifter_1_out), .out(adder_2_out));  // open: cin, cout
  Multiplexer #(.width(32), .enable("false")) multiplexer_1 (
    .in0(adder_1_out), .in1(adder_2_out), .out(multiplexer_1_out), .sel(Branch));
  // MIPSProgramROM mipsprogramrom_1: pin names not known; wires that end beside it: PC_q, mipsprogramrom_1_p2
  Register #(.width(32)) IF_ID (
    .D(mipsprogramrom_1_p2), .en(1'b1), .clk(clock_1_out), .Q({IF_ID_q[31:26], AddrA, AddrB, IF_ID_q[15:0]}),
    .clr(RESET));
  Multiplexer #(.width(5), .enable("false")) multiplexer_2 (
    .in0(AddrB), .in1(IF_ID_q[15:11]), .out(AddrW), .sel(RegDst));
  assign bit_extender_1_out = {{16{IF_ID_q[15]}}, IF_ID_q[15:0]};  // Bit_Extender bit_extender_1
  Clock clock_1 (.out(clock_1_out));
  // RegisterFile registerfile_1: pin names not known; wires that end beside it: registerfile_1_p1, clock_1_out, RegWrite, registerfile_1_p4, AddrA, AddrB, registerfile_1_p7, registerfile_1_p8
  Shifter #(.width(32)) shifter_1 (.in(bit_extender_1_out), .\dist (5'b00010), .out(shifter_1_out));
  Register #(.width(32)) ID_EX (.D(registerfile_1_p7), .en(1'b1), .clk(clock_1_out), .Q(ID_EX_q), .clr(RESET));
  Register #(.width(32)) register_1 (
    .D(registerfile_1_p8), .en(1'b1), .clk(clock_1_out), .Q(register_1_q), .clr(RESET));
  Register #(.width(32)) register_2 (
    .D(bit_extender_1_out), .en(1'b1), .clk(clock_1_out), .Q(register_2_q), .clr(RESET));
  Register #(.width(5)) register_3 (.D(AddrW), .en(1'b1), .clk(clock_1_out), .Q(register_3_q), .clr(RESET));
  Multiplexer #(.width(32), .enable("false")) multiplexer_3 (
    .in0(register_1_q), .in1(register_2_q), .out(multiplexer_3_out), .sel(ALUScr));
  Multiplexer #(.select(2), .width(32), .enable("false")) multiplexer_4 (
    .in0(ID_EX_q), .in1(EX_MEM_q), .out(A), .sel(in_1));  // open: in2, in3
  Multiplexer #(.select(2), .width(32), .enable("false")) multiplexer_5 (
    .in0(multiplexer_3_out), .in1(EX_MEM_q), .out(B), .sel(in_2));  // open: in2, in3
  // Mips_ALU mips_alu_1: pin names not known; wires that end beside it: A, B, ALUOp, mips_alu_1_p4
  Register #(.width(32)) EX_MEM (.D(mips_alu_1_p4), .en(1'b1), .clk(clock_1_out), .Q(EX_MEM_q), .clr(RESET));
  Register #(.width(32)) register_4 (.D(register_1_q), .en(1'b1), .clk(clock_1_out), .Q(register_4_q), .clr(RESET));
  Register #(.width(5)) register_5 (.D(register_3_q), .en(1'b1), .clk(clock_1_out), .Q(register_5_q), .clr(RESET));
  // MIPS_RAM mips_ram_1: pin names not known; wires that end beside it: EX_MEM_q[19:0], register_4_q, MemWrite, 4'b1111, clock_1_out, MemRead, RESET, mips_ram_1_p8, mips_ram_1_p8, mips_ram_1_p10
  Multiplexer #(.width(32), .enable("false")) multiplexer_6 (
    .in0(mips_ram_1_p10), .in1(EX_MEM_q), .out(multiplexer_6_out), .sel(MemToReg));
  Register #(.width(32)) MEM_WB (
    .D(multiplexer_6_out), .en(1'b1), .clk(clock_1_out), .Q(registerfile_1_p1), .clr(RESET));
  Register #(.width(5)) register_6 (.D(register_5_q), .en(1'b1), .clk(clock_1_out), .Q(registerfile_1_p4), .clr(RESET));

  // Notes on the sheet:
  //   contents of mipsprogramrom_1 (hex, n*v repeats v):
  //   subu $9,$16,$10 addu $9,$8,$8 addiu $9,$10,30
endmodule
